// Digital circuit autofetch.dig as structural Verilog
module autofetch (
  input  CLK,
  input  CR,
  output [3:0] \µstep ,
  output fetch_1,
  output fetch_3,
  output fetch_2
);

  wire d_ff_1_nq, d_ff_1_q, decoder_1_out_3;
  wire [1:0] counter_1_out;

  Counter #(.Bits(2)) counter_1 (.en(d_ff_1_nq), .C(CLK), .clr(CR), .out(counter_1_out));  // open: ovf
  Decoder #(.Selector_Bits(2)) decoder_1 (
    .sel(counter_1_out), .out_0(fetch_1), .out_1(fetch_2), .out_2(fetch_3), .out_3(decoder_1_out_3));
  D_FF d_ff_1 (.D(decoder_1_out_3), .C(~CLK), .Q(d_ff_1_q), .nQ(d_ff_1_nq));
  Counter #(.Bits(4)) counter_2 (.en(d_ff_1_q), .C(CLK), .clr(CR), .out(\µstep ));  // open: ovf
endmodule
